# Fritzing sketch v2 (saved by Fritzing 0.7.11b)
breadboards: 2

parts:
  WM8731 = SSOP28DB [chip_label=IC part_number=WM8731 package=SSOP]
  ACHL = IC, DIP package, 8 pins [chip_label=IC part_number=ACHL-24088]
  Vreg = IC, SIP package, 3 pins [chip_label=IC part_number=LD1117V33]
  DC_Power1 = DC Power [voltage=5]
  SPI = female pin header, 3 pins [form="♀ (female)"]
  AUDIO = female pin header, 5 pins [form="♀ (female)"]
  POWER = female pin header, 2 pins [form="♀ (female)"]
  R2 = Resistor [tolerance=±5% resistance=10k package="0603 [SMD]"]
  R3 = Resistor [tolerance=±5% resistance=10k package="0603 [SMD]"]
  R1 = Resistor [tolerance=±5% resistance=10k package="0603 [SMD]"]
  C3 = Electrolytic Capacitor [capacitance=0.22mF voltage=6.3V package="0405 [SMD, electrolytic]"]
  C2 = Electrolytic Capacitor [capacitance=0.22mF voltage=6.3V package="0405 [SMD, electrolytic]"]
  C1 = Electrolytic Capacitor [capacitance=10µF package="0405 [SMD, electrolytic]"]
  HP_OUT = Stereo Jack (TRS) 3.5mm [package="PG203J [THT]"]

nets:
  3.3V: WM8731.1, WM8731.8, WM8731.14, WM8731.27, ACHL.pin8, Vreg.pin2, R1.Pin_0, C1.+
  N1: WM8731.3, AUDIO.pin5
  N2: WM8731.4, AUDIO.pin4
  N3: WM8731.5, AUDIO.pin3
  N4: WM8731.6, AUDIO.pin2
  N5: WM8731.7, AUDIO.pin1
  N6: WM8731.9, C3.+
  N7: WM8731.10, C2.+
  GND: WM8731.11, WM8731.15, WM8731.28, ACHL.pin4, Vreg.pin1, DC_Power1.GND, POWER.pin1, R2.Pin_1, R3.Pin_1, C1.-, HP_OUT.Sleeve
  N8: WM8731.21, R1.Pin_1
  N9: WM8731.22, SPI.pin1
  N10: WM8731.23, SPI.pin2
  N11: WM8731.24, SPI.pin3
  N12: WM8731.25, ACHL.pin5
  N13: Vreg.pin3, DC_Power1.V+, POWER.pin2
  N14: R2.Pin_0, C2.-, HP_OUT.Ring
  N15: R3.Pin_0, C3.-, HP_OUT.Tip
